# Fritzing sketch MINI MAGNETIC REED (saved by Fritzing 0.9.3b)

parts:
  MH-ET_LIVE_ESP32_DEVKIT1 = MH-ET LIVE ESP32 DEVKIT 38 pins
  Mod1 = KY-021 Mini Magnetic Reed Switch Module [package="Breakout board"]

nets:
  N1: MH-ET_LIVE_ESP32_DEVKIT1.IO33, Mod1.S
  5V: MH-ET_LIVE_ESP32_DEVKIT1.5V, Mod1.Vin
  N2: MH-ET_LIVE_ESP32_DEVKIT1.GND, Mod1.-

custom parts:
  MH-ET LIVE ESP32 DEVKIT 38 pins: http://mh.nodebb.com/topic/2/mh-et-live-esp32-devkit
  KY-021 Mini Magnetic Reed Switch Module: KY-021 magnetic reed switch module. A reed switch is a magnetic sensor that is normally open and gets closed when exposed to a magnetic field.

// code stored in the sketch: MINI MAGNETIC REED.ino
const int sensorPin = 2; // Pin al que está conectado el sensor
int valorSensor = 0; // Variable para almacenar el valor del sensor

void setup() {
  pinMode(sensorPin, INPUT); // Establecer el pin como entrada
  Serial.begin(9600); // Iniciar la comunicación serial
}

void loop() {
  valorSensor = digitalRead(sensorPin); // Leer el valor del sensor

  if (valorSensor == HIGH) { // Si el sensor está activado
    Serial.println("¡Sensor activado!"); // Imprimir un mensaje en la consola
  }

  delay(10); // Pequeña pausa entre lecturas del sensor
}
