# Fritzing sketch Relé sensor (saved by Fritzing 0.9.3b)

parts:
  KY-1 = Keyes Relay [package=THT]
  U1 = ESP32-38PinWide [part_number=ESP32-38PinWide]

nets:
  N1: KY-1.signal, U1.GPIO23
  N2: KY-1.power, U1.VIN
  N3: KY-1.ground, U1.GND

custom parts:
  Keyes Relay: The Keyes 5V relay module is suitable for SCM development, home appliance control. It uses a 5V~12V TIL control signal which can control DC / AC signal.
  ESP32-38PinWide: Generic 38-Pin ESP32 with wide format (only access to one side of pins on a breadboard) based on Stephen Lilley's HiLetgo ESP-WROOM-32 ESP32 ESP-32S Development Board.

// code stored in the sketch: RelΘ sensor.ino

const int relayPin = 5; // Pin del módulo de relé


bool relayState = false; // Variable para almacenar el estado del relé



void setup() {

  pinMode(relayPin, OUTPUT); // Configurar el pin del relé como salida

  Serial.begin(9600); // Inicializar la comunicación serial

}



void loop() {

  if (relayState == false) { // Si el relé está apagado

    digitalWrite(relayPin, HIGH); // Encender el relé

    Serial.println("Relé encendido"); // Imprimir un mensaje por el puerto serial

    relayState = true; // Actualizar el estado del relé

  } else { // Si el relé está encendido

    digitalWrite(relayPin, LOW); // Apagar el relé

    Serial.println("Relé apagado"); // Imprimir un mensaje por el puerto serial

    relayState = false; // Actualizar el estado del relé

  }



  delay(1000); // Pequeña pausa para que se pueda apreciar el cambio de estado del relé

}
