# Fritzing sketch Sensor de golpe (saved by Fritzing 0.9.3b)

parts:
  U2 = ESP32-38PinWide [part_number=ESP32-38PinWide]
  Mod2 = KY-031 Knock Sensor Module [package="Breakout board"]

nets:
  VIN: U2.VIN, Mod2.Vin
  N1: U2.GPIO16, Mod2.S
  N2: U2.GND, Mod2.-

custom parts:
  ESP32-38PinWide: Generic 38-Pin ESP32 with wide format (only access to one side of pins on a breadboard) based on Stephen Lilley's HiLetgo ESP-WROOM-32 ESP32 ESP-32S Development Board.
  KY-031 Knock Sensor Module: KY-031 Knock Sensor module. A vibration sensor that sends a signal when a knock/tap is detected.

// code stored in the sketch: Sensor de golpe.ino
const int sensorPin = 16; // Pino al que está conectado el sensor
int valorSensor = 0; // Variable para almacenar el valor del sensor

void setup() {
  pinMode(sensorPin, INPUT); // Establecer el pin como entrada
  Serial.begin(9600); // Iniciar la comunicación serial
}

void loop() {
  valorSensor = digitalRead(sensorPin); // Leer el valor del sensor

  if (valorSensor == HIGH) { // Si el sensor detecta un golpe
    Serial.println("¡Golpe detectado!"); // Imprimir un mensaje en la consola
  }

  delay(10); // Pequeña pausa entre lecturas del sensor
}
